// Logisim project Project2.circ as structural Verilog
module main (
);

  Button one ();  // open: out
  Button four ();  // open: out
  Button seven ();  // open: out
  Button L ();  // open: out
  Button two ();  // open: out
  Button five ();  // open: out
  Button eight ();  // open: out
  Button zero ();  // open: out
  Button three ();  // open: out
  Button six ();  // open: out
  Button nine ();  // open: out
  Button U ();  // open: out
endmodule

module Panel (
  input  R0,
  input  R1,
  input  R2,
  input  R3,
  input  C0,
  input  C1,
  input  C2,
  output B3,
  output B2,
  output B1,
  output B0,
  output V
);

  wire Eight, Five, Four, L, Nine, One, priority_encoder_1_gs, Seven, Six, Three, Two, U, xor_1_out,
       xor_2_out, Zero;
  wire [3:0] multiplexer_1_out, priority_encoder_1_out;

  and and_1 (One, R0, C0);
  and and_2 (Two, R0, C1);
  and and_3 (Three, R0, C2);
  and and_4 (L, R3, C0);
  and and_5 (U, R3, C2);
  and and_6 (Four, R1, C0);
  and and_7 (Five, R1, C1);
  and and_8 (Six, R1, C2);
  and and_9 (Zero, R3, C1);
  and and_10 (Seven, R2, C0);
  and and_11 (Eight, R2, C1);
  and and_12 (Nine, R2, C2);
  Priority_Encoder #(.select(4)) priority_encoder_1 (
    .in0(Zero), .in1(One), .in2(Two), .in3(Three), .in4(Four), .in5(Five), .in6(Six), .in7(Seven),
    .in8(Eight), .in9(Nine), .in10(L), .in11(U), .out(priority_encoder_1_out), .gs(priority_encoder_1_gs));  // open: in12, in13, in14, in15, en_out, en_in
  Multiplexer #(.width(4)) multiplexer_1 (
    .in1(priority_encoder_1_out), .out(multiplexer_1_out), .sel(priority_encoder_1_gs));  // open: in0
  ExactlyOne xor_1 (.out(xor_1_out), .in0(R0), .in1(R1), .in2(R2), .in3(R3));
  ExactlyOne xor_2 (.out(xor_2_out), .in0(C0), .in1(C1), .in2(C2));
  ExactlyOne xor_3 (.out(B3), .in0(Eight), .in1(Nine), .in2(L), .in3(Zero), .in4(U));
  ExactlyOne xor_4 (.out(B2), .in0(Four), .in1(Five), .in2(Six), .in3(Seven));
  ExactlyOne xor_5 (.out(B1), .in0(L), .in1(U), .in2(Two), .in3(Six), .in4(Three), .in5(Seven));
  ExactlyOne xor_6 (.out(B0), .in0(Three), .in1(Seven), .in2(Five), .in3(Nine), .in4(U), .in5(One));
  and and_13 (V, xor_1_out, xor_2_out);
endmodule

module InputBuffer (
  input  B0,
  input  B1,
  input  B2,
  input  B3,
  input  V,
  output [3:0] out_6,
  output [3:0] out_7,
  output C0,
  output C1,
  output C2,
  output C3
);

  wire and_1_out, CLK, d_ff_1_qn;

  Clock u_CLK (.out(CLK));
  D_Flip_Flop d_ff_1 (.D(V), .clk(CLK), .Qn(d_ff_1_qn));  // open: Q, preset, reset
  Multiplexer #(.width(4)) multiplexer_1 (.in0(4'b1111), .in1({B3, B2, B1, B0}), .out(out_6), .sel(and_1_out));
  and and_1 (and_1_out, d_ff_1_qn, V);
  Register #(.width(4)) register_1 (.D(out_6), .en(1'b1), .clk(CLK), .Q({C3, C2, C1, C0}));  // open: clr

  assign out_7 = {C3, C2, C1, C0};
endmodule
